// Logisim project 6502.circ as structural Verilog
module COMPUTER (
);

  wire BTN_RST_out, CLK, rst;

  Button BTN_RST (.out(BTN_RST_out));
  Clock u_CLK (.out(CLK));
  RAM ram_1 ();  // open: ADR, CLK, DIN, WRMEM, RDMEM, rst, DOUT, fc
  // RisingEdge risingedge_1: pin names not known; wires that end beside it: BTN_RST_out, CLK, rst
endmodule

module RAM (
  input  [15:0] ADR,
  input  CLK,
  input  [7:0] DIN,
  input  WRMEM,
  input  RDMEM,
  input  rst,
  output [7:0] DOUT,
  output fc
);

  wire and_1_out, and_2_out, CNT0, LDCNT, not_1_out, notCNT0, or_1_out, reg4_ld_sl_sr_1_p6, rsff_2_p4,
       rsff_2_p5, rsff_3_p4, sl;
  wire [3:0] CNT, LFSR;

  // RSFF rsff_1: pin names not known; wires that end beside it: 1'b0, CLK, rst, sl
  or or_1 (or_1_out, WRMEM, RDMEM);
  // REG4_LD_SL_SR reg4_ld_sl_sr_1: pin names not known; wires that end beside it: 1'b0, 1'b0, CLK, 4'b1111, LFSR, reg4_ld_sl_sr_1_p6, sl, rst
  // RisingEdge risingedge_1: pin names not known; wires that end beside it: or_1_out, CLK, LDCNT
  // MEM64Kx8 mem64kx8_1: pin names not known; wires that end beside it: ADR, 1'b1, CLK, DIN, DOUT, WRMEM
  xor xor_1 (reg4_ld_sl_sr_1_p6, LFSR[2], LFSR[3]);
  not not_1 (not_1_out, LDCNT);
  and and_1 (and_1_out, CNT0, not_1_out);
  // REG4m_DEC_LD reg4m_dec_ld_1: pin names not known; wires that end beside it: CLK, LFSR, CNT, LDCNT, notCNT0, notCNT0
  // RSFF rsff_2: pin names not known; wires that end beside it: and_1_out, CLK, LDCNT, rsff_2_p4, rsff_2_p5
  not not_2 (rsff_2_p4, rst);
  or or_2 (notCNT0, CNT[0], CNT[1], CNT[2], CNT[3]);
  not not_3 (CNT0, notCNT0);
  and and_2 (and_2_out, rsff_2_p5, CNT0);
  // RSFF rsff_3: pin names not known; wires that end beside it: fc, CLK, and_2_out, rsff_3_p4, fc
  not not_4 (rsff_3_p4, rst);
endmodule
